// Logisim project ULA.circ as structural Verilog: 3 circuits, main circuit main
module main (
  input  [31:0] Entrada_A,
  input  [31:0] Entrada_B,
  input  [4:0] Seletor,
  output Overflow,
  output [31:0] \Saída_S 
);

  wire Overflow_overflow, undriven, undriven_3, undriven_4, undriven_5;
  wire [4:0] undriven_2;

  Celula celula_1 ();  // open: Cin, SLL, a, b, Seletor, S, SRL, Cout
  OverFlowControler u_Overflow (
    .Overflow(Overflow_overflow), .Cin(undriven), .Seletor(undriven_2), .a(undriven_3), .b(undriven_4),
    .s(undriven_5));

  // Notes on the sheet:
  //   00000=AND
  //   00001=OR
  //   00010=XOR
  //   00011=NAND
  //   00100=SOMA INT
  //   00101=SOMA NAT
  //   00110=SUBTRAIR
endmodule

module Celula (
  input  Cin,
  input  SLL,
  input  SRL,
  input  a,
  input  b,
  input  [4:0] Seletor,
  output S,
  output Cout
);

  wire adder_1_cout, adder_1_out, and_1_out, and_2_out, nand_1_out, or_1_out, subtractor_1_bout,
       subtractor_1_out, xor_1_out;

  and and_1 (and_1_out, b, a);
  or or_1 (or_1_out, b, a);
  xor xor_1 (xor_1_out, b, a);
  nand nand_1 (nand_1_out, b, a);
  Adder #(.width(1)) adder_1 (.a(a), .b(b), .out(adder_1_out), .cin(Cin), .cout(adder_1_cout));
  Subtractor #(.width(1)) subtractor_1 (.a(a), .b(b), .out(subtractor_1_out), .bin(Cin), .bout(subtractor_1_bout));
  Multiplexer #(.enable("false")) multiplexer_1 (
    .in0(adder_1_cout), .in1(subtractor_1_bout), .out(Cout), .sel(and_2_out));
  and and_2 (and_2_out, ~Seletor[0], Seletor[1], Seletor[2], ~Seletor[3], ~Seletor[4]);  // AND_Gate
  Multiplexer #(.select(5), .enable("false")) multiplexer_2 (
    .in0(and_1_out), .in1(or_1_out), .in2(xor_1_out), .in3(nand_1_out), .in4(adder_1_out), .in5(adder_1_out),
    .in6(subtractor_1_out), .in7(SLL), .in8(SRL), .out(S), .sel(Seletor));  // open: in9, in10, in11, in12, in13, in14, in15, in16, in17, in18, in19, in20, in21, in22, in23, in24, in25, in26, in27, in28, in29, in30, in31

  // Notes on the sheet:
  //   00000=AND
  //   00001=OR
  //   00010=XOR
  //   00011=NAND
  //   00100=SOMA INT
  //   00101=SOMA NAT
  //   00110=SUBTRATOR
  //   00111=DESLOCAMENTO ESQUERDA
  //   01000=DESLOCAMENTO DIREITA
endmodule

module OverFlowControler (
  input  Cin,
  input  a,
  input  b,
  input  s,
  input  [4:0] Seletor,
  output Overflow
);

  wire and_1_out, and_2_out, and_3_out, or_1_out;

  Multiplexer #(.enable("false")) multiplexer_1 (.in0(Cin), .in1(or_1_out), .out(Overflow), .sel(and_1_out));
  and and_1 (and_1_out, Seletor[0], ~Seletor[1], Seletor[2], ~Seletor[3], ~Seletor[4]);  // AND_Gate
  or or_1 (or_1_out, and_2_out, and_3_out);
  and and_2 (and_2_out, a, b, ~s);  // AND_Gate
  and and_3 (and_3_out, ~a, ~b, s);  // AND_Gate

  // Notes on the sheet:
  //   00100 - Soma de Naturais
  //   00101 - Soma de Inteiros
endmodule
